# Fritzing sketch engine (saved by Fritzing 0.9.3b)
breadboards: 1

parts:
  Raspberry_Pi_1 = Raspberry Pi 3 [part_number=RPI-3-V1.2]
  IC1 = L293D [package=THT]
  M1 = DC Motor
  M2 = DC Motor
  Part2 = Lithium Ion Cylindrical Battery 3.7v 2200mAh [part_number=1781]

nets:
  N1: Raspberry_Pi_1.GIPO5, IC1.In_2
  N2: Raspberry_Pi_1.GIPO6, IC1.In_1
  N3: Raspberry_Pi_1.GIPO13, IC1.Enable_1
  N4: Raspberry_Pi_1.GND, IC1.0V, Part2.negative
  N5: Raspberry_Pi_1.GIPO20, IC1.In_3
  N6: Raspberry_Pi_1.GIPO16, IC1.In_4
  N7: Raspberry_Pi_1.GIPO12, IC1.Enable_2
  N8: Raspberry_Pi_1.5V, IC1.+V
  N9: IC1.Out_1_(_Controlled_by_Enable_1_), M2.pin_2
  N10: IC1.Out_2_(_Controlled_by_Enable_1_), M2.pin_1
  N11: IC1.+Vmotor, Part2.positive
  N12: IC1.Out_3_(_Controlled_by_Enable_2_), M1.pin_2
  N13: IC1.Out_4_(_Controlled_by_Enable_2_), M1.pin_1

custom parts:
  Lithium Ion Cylindrical Battery 3.7v 2200mAh: This lithium ion battery has a capacity of 2200mAh and a protection circuit that provides over-voltage, under-voltage and over-current protection. This cell can provide 2C of peak current (4400mA). Note that these batteries are not designed to sustain such high loads, we suggest keeping any constant current draw under about 0.5C (1 Amp).
